// Logisim project IT012_Lab01_25520635.circ as structural Verilog: 6 circuits, main circuit TN1
module TN1 (
  input  A,
  input  B,
  input  C,
  output A_prime,
  output AB,
  output A_B,
  output CHAIN,
  output NAND_A_B,
  output NOR_A_B,
  output XOR_A_B,
  output XNOR_A_B,
  output XOR3,
  output NAND3
);

  not not_1 (A_prime, A);
  and and_1 (AB, A, B);
  or or_1 (A_B, A, B);
  nand nand_1 (NAND_A_B, A, B);
  nor nor_1 (NOR_A_B, A, B);
  xor xor_1 (XOR_A_B, A, B);
  xnor xnor_1 (XNOR_A_B, A, B);
  ExactlyOne xor_2 (.out(XOR3), .in0(A), .in1(B), .in2(C));
  nand nand_2 (NAND3, A, B, C);
  nand nand_3 (CHAIN, C, NAND_A_B);
endmodule

module TN2 (
  input  x,
  input  y,
  input  z,
  output EQ1,
  output EQ2,
  output EQ3,
  output EQ4,
  output EQ5
);

  wire not_1_out, not_2_out, x___x_prime_y_out, x___yz_out, x__x_prime_y_out, x__y__prime_out, x_prime_2_out,
       x_prime___y_prime_2_out, x_prime___y_prime_out, x_prime_out, x_prime_y_2_out, x_prime_y_out,
       x_y_2_out, x_y___x_z_out, x_y_out, x_z_out, xy__prime_out, yz_out;

  not not_1 (not_1_out, y);
  not not_2 (not_2_out, x);
  not x_prime (x_prime_out, x);
  not x_prime_2 (x_prime_2_out, x);
  nor x__y__prime (x__y__prime_out, x, y);
  and x_prime___y_prime (x_prime___y_prime_out, not_1_out, not_2_out);
  nand xy__prime (xy__prime_out, y, x);
  and x_prime___y_prime_2 (x_prime___y_prime_2_out, not_1_out, not_2_out);
  and yz (yz_out, y, z);
  or x_y (x_y_out, x, y);
  or x_z (x_z_out, x, z);
  and x_prime_y (x_prime_y_out, x_prime_out, y);
  and x_prime_y_2 (x_prime_y_2_out, x_prime_2_out, y);
  or x___yz (x___yz_out, yz_out, x);
  and x_y___x_z (x_y___x_z_out, x_y_out, x_z_out);
  or x___x_prime_y (x___x_prime_y_out, x_prime_y_out, x);
  or x__x_prime_y (x__x_prime_y_out, x_prime_y_2_out, x);
  or x_y_2 (x_y_2_out, x, y);
  xnor xnor_1 (EQ1, x__y__prime_out, x_prime___y_prime_out);
  xnor xnor_2 (EQ2, xy__prime_out, x_prime___y_prime_2_out);
  xnor xnor_3 (EQ3, x___yz_out, x_y___x_z_out);
  xnor xnor_4 (EQ4, x___x_prime_y_out, x);
  xnor xnor_5 (EQ5, x__x_prime_y_out, x_y_2_out);
endmodule

module TN3 (
  input  A,
  input  B,
  input  C,
  input  D,
  output F
);

  wire and_1_out, and_2_out, and_3_out, and_4_out, and_5_out, and_6_out, not_1_out, not_2_out, not_3_out,
       not_4_out;

  not not_1 (not_1_out, A);
  not not_2 (not_2_out, B);
  not not_3 (not_3_out, C);
  not not_4 (not_4_out, D);
  and and_1 (and_1_out, not_1_out, not_2_out, C, not_4_out);
  and and_2 (and_2_out, not_1_out, not_2_out, C, D);
  and and_3 (and_3_out, not_1_out, B, not_3_out, D);
  or or_1 (F, and_1_out, and_2_out, and_3_out, and_4_out, and_5_out, and_6_out);
  and and_4 (and_4_out, not_1_out, B, C, D);
  and and_5 (and_5_out, A, not_2_out, C, D);
  and and_6 (and_6_out, A, B, not_3_out, D);
endmodule

module TN4 (
  input  A,
  input  B,
  input  C,
  input  D,
  output F_SoP,
  output F_PoS,
  output F_can,
  output EQ1,
  output EQ2
);

  wire and_1_out, and_2_out, and_3_out, and_4_out, and_5_out, and_6_out, and_7_out, and_8_out, and_9_out,
       and_10_out, not_1_out, not_2_out, not_3_out, not_4_out, or_3_out, or_4_out, or_5_out, or_6_out,
       or_7_out;

  not not_1 (not_1_out, A);
  not not_2 (not_2_out, B);
  not not_3 (not_3_out, C);
  not not_4 (not_4_out, D);
  and and_1 (and_1_out, not_1_out, not_2_out, C, not_4_out);
  and and_2 (and_2_out, not_1_out, not_2_out, C, D);
  and and_3 (and_3_out, not_1_out, B, not_3_out, D);
  or or_1 (F_can, and_1_out, and_2_out, and_3_out, and_4_out, and_5_out, and_6_out);
  and and_4 (and_4_out, not_1_out, B, C, D);
  and and_5 (and_5_out, A, not_2_out, C, D);
  and and_6 (and_6_out, A, B, not_3_out, D);
  xnor xnor_1 (EQ1, F_can, F_SoP);
  and and_7 (and_7_out, not_1_out, not_2_out, C);
  and and_8 (and_8_out, not_1_out, B, D);
  and and_9 (and_9_out, not_2_out, C, D);
  and and_10 (and_10_out, B, not_3_out, D);
  or or_2 (F_SoP, and_7_out, and_8_out, and_10_out, and_9_out);
  xnor xnor_2 (EQ2, F_can, F_PoS);
  or or_3 (or_3_out, B, C);
  or or_4 (or_4_out, C, D);
  or or_5 (or_5_out, not_2_out, D);
  and and_11 (F_PoS, or_3_out, or_4_out, or_5_out, or_6_out, or_7_out);
  or or_6 (or_6_out, not_1_out, D);
  or or_7 (or_7_out, not_1_out, not_2_out, not_3_out);
endmodule

module TN5 (
  input  A,
  input  B,
  input  C,
  output F
);

  wire xor_1_out;

  xor xor_1 (xor_1_out, B, A);
  xor xor_2 (F, C, xor_1_out);
endmodule

module Warmup (
  input  A,
  input  B,
  output AB_prime
);

  wire not_1_out;

  not not_1 (not_1_out, B);
  and and_1 (AB_prime, not_1_out, A);
endmodule
